# Fritzing sketch color-match-strip (saved by Fritzing 0.9.3b)
breadboards: 1

parts:
  Part1 = Adafruit Pro Trinket 5V 16MHz [part_number="Adafruit #2000"]
  Part2 = Adafruit TCS34725 RGB Color Sensor [part_number="Adafruit #1334"]
  NEOPIXEL1 = Neopixel Strip -- White (30/m)

nets:
  GND: Part1.GND, Part2.GND, Part2.LED_EN, NEOPIXEL1.GND
  +5V: Part1.+5V, Part2.VIN, NEOPIXEL1.+5V
  N1: Part1.D6, NEOPIXEL1.Din
  N2: Part1.A4, Part2.SDA
  N3: Part1.A5, Part2.SCL

custom parts:
  Adafruit Pro Trinket 5V 16MHz: Trinket's got a big sister in town - the Pro Trinket 5V! Pro Trinket combines everything you love about Trinket with the familiarity of the common core Arduino chip, the ATmega328. It's like an Arduino Pro Mini with more pins and USB tossed in, so delicious. Trinket's a year old now, and while its been great to see tons of tiny projects, sometimes you just need more pins, more FLASH, and more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
  Adafruit TCS34725 RGB Color Sensor: Your electronics can now see in dazzling color with this lovely color light sensor. We found the best color sensor on the market, the TCS34725, which has RGB and Clear light sensing elements. An IR blocking filter, integrated on-chip and localized to the color sensing photodiodes, minimizes the IR spectral component of the incoming light and allows color measurements to be made accurately. The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
  Neopixel Strip -- White (30/m): These NeoPixel strips have 30 digitally-addressable pixel LEDs per meter and are very affordable and are only 12.5 mm wide, 10 mm if you remove the strip from the casing.
